# Fritzing sketch G11_Project_RoboPet_2 (saved by Fritzing 1.0.0d)
breadboards: 2

parts:
  J1 = Basic Servo
  J2 = Basic Servo
  J3 = Basic Servo
  J4 = Basic Servo
  Part1 = RFID-RC522-v2
  Mod1 = Raspberry Pi Pico W
  J5 = Piezo Speaker
  C1 = Electrolytic Capacitor [capacitance=1µF voltage=35V package="100 mil [THT, electrolytic]"]
  R1 = Resistor [tolerance=±5% power=0.25W resistance=220 package=THT]
  R2 = Resistor [tolerance=±5% power=0.25W resistance=220 package=THT]
  R3 = Resistor [tolerance=±5% power=0.25W resistance=220 package=THT]
  LED1 = RGB LED (com. cathode, rbg) [color="Red (633nm)" current=0.030A package="5 mm [THT]"]
  VCC1 = 4 x AAA Battery Mount

nets:
  GND: J1.gnd, J2.gnd, J3.gnd, J4.gnd, Part1.GND, Mod1.pin_3, Mod1.pin_8, Mod1.pin_13, Mod1.pin_18, Mod1.pin_23, Mod1.pin_28, Mod1.pin_33, Mod1.pin_38, Mod1.pin_42, J5.pin1, C1.-, LED1.common_cathode, VCC1.-
  VCC: J1.vcc, J2.vcc, J3.vcc, J4.vcc, Mod1.pin_39, C1.+, VCC1.+
  N1: J1.pulse, Mod1.pin_26
  N2: J2.pulse, Mod1.pin_25
  N3: J3.pulse, Mod1.pin_29
  N4: J4.pulse, Mod1.pin_27
  N5: Part1.SDA, Mod1.pin_2
  N6: Part1.SCK, Mod1.pin_4
  N7: Part1.MOSI, Mod1.pin_5
  N8: Part1.MISO, Mod1.pin_6
  N9: Part1.RST, Mod1.pin_1
  N10: Part1.3.3V, Mod1.pin_36
  N11: Mod1.pin_14, J5.pin2
  N12: Mod1.pin_15, R3.Pin_0
  N13: Mod1.pin_16, R2.Pin_1
  N14: Mod1.pin_17, R1.Pin_0
  N15: R1.Pin_1, LED1.blue_anode
  N16: R2.Pin_0, LED1.green_anode
  N17: R3.Pin_1, LED1.red_anode

custom parts:
  RFID-RC522-v2: A simple China made RFID-RC522 Reader; do check the pin labels, as this is a MFRC522 based clone.
  Raspberry Pi Pico W: Raspberry Pi Pico W. Based around the RP2040 microcontroller the Pico W is a low cost microcontroller device bringing Raspberry Pi quality, cost, and easy of use to the microcontroller space. The areas marked KEEPOUT in pcb silkscreen should not have traces running through them to avoid shorts on a soldered in module!
